# Fritzing sketch HSS_node_4send (saved by Fritzing 0.9.2b)
breadboards: 1

parts:
  Part1 = Arduino Pro Mini v13
  VCC2 = Battery
  U1 = Voltage Regulator - 5V [package="TO220 [THT]"]
  REG1 = LD33 Low-Dropout Voltage Regulator
  NRF24L1 = NRF24L01
  NOR_GATE_-_CD4001BE1 = SN74LS14N [package="DIP14 [THT]"]
  U2 = SM130 [package=sm130]
  Part2 = Logic Level Converter
  R1 = Resistor [tolerance=±5% resistance=220 package=THT]
  S1 = Reed switch [package=THT]
  R2 = Resistor [tolerance=±5% resistance=220 package=THT]
  S2 = Reed switch [package=THT]
  PIR1 = PIR sensor

nets:
  VCC: Part1.VCC, REG1.Vout, NRF24L1.VCC, NOR_GATE_-_CD4001BE1.VCC, U2.VCC, Part2.LV, R1.Pin_0, R2.Pin_0
  GND: Part1.GND, VCC2.-, U1.GND, REG1.GND, NRF24L1.GND, NOR_GATE_-_CD4001BE1.GND, U2.GND, Part2.GND, S1.pin_1, S2.pin_1, PIR1.GND
  N1: Part1.D13/SCK, NRF24L1.SCK
  N2: Part1.D12/MISO, NRF24L1.MISO
  N3: Part1.D11_PWM/MOSI, NRF24L1.MOSI
  N4: Part1.D10_PWM/SS, NRF24L1.CSN
  N5: Part1.D9_PWM, NRF24L1.CE
  N6: Part1.D4, NOR_GATE_-_CD4001BE1.4A, Part2.RX_HV
  N7: Part1.D3_PWM, NOR_GATE_-_CD4001BE1.2A
  N8: Part1.D2, NRF24L1.IRQ, NOR_GATE_-_CD4001BE1.5Y
  N9: VCC2.+, U1.input_voltage, REG1.Vin
  N10: U1.output_voltage, Part2.HV, PIR1.VDD
  N11: NOR_GATE_-_CD4001BE1.1A, R2.Pin_1, S2.pin_2
  N12: NOR_GATE_-_CD4001BE1.1Y, PIR1.SIG
  N13: NOR_GATE_-_CD4001BE1.4Y, R1.Pin_1, S1.pin_2
  N14: U2.ANT1, Part2.TX_LV

custom parts:
  NRF24L01: NRF24L01 module
