# Fritzing sketch HSS_node_accumulator (saved by Fritzing 0.9.2b)
circuit board: 8.46667cm x 5.64444cm
breadboards: 1

parts:
  NOR_GATE_-_CD4001BE = SN74LS14N [package="DIP14 [THT]"]
  C1 = Electrolytic Capacitor [capacitance=1µF package="100 mil [THT, electrolytic]"]
  S1 = Reed switch [package=THT]
  R1 = Resistor [tolerance=±5% resistance=220 package=THT]
  PIR1 = PIR sensor
  NRF24L2 = NRF24L01
  Part2 = Arduino Pro Mini v13
  J1 = Piezo Speaker
  R2 = Resistor [tolerance=±5% resistance=220 package=THT]
  REG1 = LD33 Low-Dropout Voltage Regulator
  VCC1 = Battery
  U1 = Voltage Regulator - 5V [package="TO220 [THT]"]
  U2 = RELAY-2 [package=relay-g5v]
  D1 = Schottky Diode [part_number=1N5817 package="300 mil [THT]"]
  Q1 = NPN-Transistor [package="TO92 [THT]"]
  1000_Ohm = Resistor [tolerance=±5% resistance=220 package=THT]

nets:
  N1: NOR_GATE_-_CD4001BE.2Y, Part2.D3_PWM
  N2: NOR_GATE_-_CD4001BE.3A, S1.pin_1, R1.Pin_0
  N3: NOR_GATE_-_CD4001BE.3Y, PIR1.SIG
  GND: NOR_GATE_-_CD4001BE.GND, C1.-, S1.pin_2, PIR1.GND, NRF24L2.GND, Part2.GND, J1.pin1, REG1.GND, VCC1.-, U1.GND, Q1.E
  VCC: NOR_GATE_-_CD4001BE.VCC, C1.+, NRF24L2.VCC, Part2.RAW, R2.Pin_1, REG1.Vout
  N4: R1.Pin_1, R2.Pin_0
  VDD: PIR1.VDD, REG1.Vin, VCC1.+, U1.input_voltage, U1.output_voltage, U2.6, U2.10, D1.cathode
  N5: NRF24L2.CSN, Part2.D10_PWM/SS
  N6: NRF24L2.MOSI, Part2.D11_PWM/MOSI
  N7: NRF24L2.IRQ, Part2.D2
  N8: NRF24L2.CE, Part2.D9_PWM
  N9: NRF24L2.SCK, Part2.D13/SCK
  N10: NRF24L2.MISO, Part2.D12/MISO
  N11: Part2.D8, 1000_Ohm.Pin_1
  N12: J1.pin2, U2.1
  N13: U2.9, D1.anode, Q1.B
  N14: Q1.C, 1000_Ohm.Pin_0

custom parts:
  NRF24L01: NRF24L01 module
