# Fritzing sketch sender2 (saved by Fritzing 0.9.2b)
breadboards: 1

parts:
  Part1 = Arduino Uno (Rev3)
  NOR_GATE_-_CD4001BE = SN74LS14N [package="DIP14 [THT]"]
  C1 = Electrolytic Capacitor [capacitance=1µF package="100 mil [THT, electrolytic]"]
  S1 = Reed switch [package=THT]
  R1 = Resistor [tolerance=±5% resistance=220 package=THT]
  R2 = Resistor [tolerance=±5% resistance=220 package=THT]
  PIR1 = PIR sensor
  NRF24L2 = NRF24L01

nets:
  N1: Part1.D9_PWM, NRF24L2.CE
  N2: Part1.D10_PWM/SS, NRF24L2.CSN
  N3: Part1.D11_PWM/MOSI, NRF24L2.MOSI
  N4: Part1.D12/MISO, NRF24L2.MISO
  N5: Part1.D13/SCK, NRF24L2.SCK
  N6: Part1.D2, NRF24L2.IRQ
  N7: Part1.D3_PWM, NOR_GATE_-_CD4001BE.2Y
  VCC: Part1.3V3, NOR_GATE_-_CD4001BE.VCC, C1.+, R2.Pin_1, NRF24L2.VCC
  5V: Part1.5V, PIR1.VDD
  GND: Part1.GND, NOR_GATE_-_CD4001BE.GND, C1.-, S1.pin_2, PIR1.GND, NRF24L2.GND
  N8: NOR_GATE_-_CD4001BE.3A, S1.pin_1, R1.Pin_0
  N9: NOR_GATE_-_CD4001BE.3Y, PIR1.SIG
  N10: R1.Pin_1, R2.Pin_0

custom parts:
  NRF24L01: NRF24L01 module
