# Fritzing sketch NOR_gate_test (saved by Fritzing 0.9.2b)
breadboards: 1

parts:
  Part1 = Arduino Uno (Rev3)
  NOR_GATE_-_CD4001BE = SN74LS14N [package="DIP14 [THT]"]
  C1 = Electrolytic Capacitor [capacitance=1µF package="100 mil [THT, electrolytic]"]
  S1 = Reed switch [package=THT]
  R1 = Resistor [tolerance=±5% resistance=220 package=THT]
  R2 = Resistor [tolerance=±5% resistance=220 package=THT]
  PIR1 = PIR sensor

nets:
  N1: Part1.D3_PWM, NOR_GATE_-_CD4001BE.2Y
  3V3: Part1.3V3, NOR_GATE_-_CD4001BE.VCC, C1.+, R2.Pin_1
  5V: Part1.5V, PIR1.VDD
  GND: Part1.GND, NOR_GATE_-_CD4001BE.GND, C1.-, S1.pin_2, PIR1.GND
  N2: NOR_GATE_-_CD4001BE.3A, S1.pin_1, R1.Pin_0
  N3: NOR_GATE_-_CD4001BE.3Y, PIR1.SIG
  N4: R1.Pin_1, R2.Pin_0
