# Fritzing sketch PIR_sensor_test_interrupt (saved by Fritzing 0.9.2b)
breadboards: 1

parts:
  PIR1 = PIR sensor
  Part1 = Arduino Uno (Rev3)

nets:
  VDD: PIR1.VDD, Part1.5V
  N1: PIR1.SIG, Part1.D3_PWM
  GND: PIR1.GND, Part1.GND
