# Fritzing sketch PIR_sensor_test_interrupt_and_sleep (saved by Fritzing 0.9.2b)
breadboards: 1

parts:
  PIR1 = PIR sensor
  Part1 = Arduino Uno (Rev3)
  U1 = INVERTER [package=sc70]

nets:
  VDD: PIR1.VDD, Part1.D3_PWM, Part1.5V, U1.A, U1.VCC
  GND: PIR1.SIG, PIR1.GND, Part1.GND, U1.GND, U1.Y
