# Fritzing sketch mag_test (saved by Fritzing 0.9.2b)
breadboards: 1

parts:
  Part1 = Arduino Uno (Rev3)
  S1 = Reed switch [package=THT]
  R1 = Resistor [tolerance=±5% resistance=220 package=THT]

nets:
  N1: Part1.D2, S1.pin_1, R1.Pin_1
  N2: Part1.5V, S1.pin_2
  N3: Part1.GND, R1.Pin_0
