# Fritzing sketch nRF24l01p_pro_mini_test_with_PIR_tx (saved by Fritzing 0.9.2b)
breadboards: 1

parts:
  Part1 = Arduino Pro Mini v13
  NRF24L1 = NRF24L01
  VCC2 = Battery block 9V
  REG2 = LD33 Low-Dropout Voltage Regulator
  PIR2 = PIR sensor

nets:
  GND: Part1.GND, NRF24L1.GND, VCC2.-, REG2.GND, REG2.Vout, PIR2.GND
  VCC: Part1.VCC, NRF24L1.VCC
  N1: Part1.D13/SCK, NRF24L1.SCK
  N2: Part1.D12/MISO, NRF24L1.MISO
  N3: Part1.D11_PWM/MOSI, NRF24L1.MOSI
  N4: Part1.D10_PWM/SS, NRF24L1.CSN
  N5: Part1.D9_PWM, NRF24L1.CE
  N6: Part1.D4, PIR2.SIG
  N7: Part1.D2, NRF24L1.IRQ
  VIN: VCC2.+, REG2.Vin, PIR2.VDD

custom parts:
  NRF24L01: NRF24L01 module
