# Fritzing sketch nRF24l01p_three_node_test_sender_PIR (saved by Fritzing 0.9.2b)
breadboards: 1

parts:
  Part1 = Arduino Pro Mini v13
  NRF24L1 = NRF24L01
  VCC2 = Battery block 9V
  REG2 = LD33 Low-Dropout Voltage Regulator
  PIR2 = PIR sensor
  R1 = Resistor [tolerance=±5% resistance=220 package=THT]
  R2 = Resistor [tolerance=±5% resistance=220 package=THT]
  LED1 = LED - 5mm [color="Red (633nm)" package="5 mm [THT]"]
  LED2 = LED - 5mm [color="Red (633nm)" package="5 mm [THT]"]

nets:
  GND: Part1.GND, NRF24L1.GND, VCC2.-, REG2.GND, REG2.Vout, PIR2.GND, LED1.cathode, LED2.cathode
  VCC: Part1.VCC, NRF24L1.VCC
  N1: Part1.D13/SCK, NRF24L1.SCK
  N2: Part1.D12/MISO, NRF24L1.MISO
  N3: Part1.D11_PWM/MOSI, NRF24L1.MOSI
  N4: Part1.D10_PWM/SS, NRF24L1.CSN
  N5: Part1.D9_PWM, NRF24L1.CE
  N6: Part1.D8, R1.Pin_1
  N7: Part1.D6_PWM, R2.Pin_0
  N8: Part1.D4, PIR2.SIG
  N9: Part1.D2, NRF24L1.IRQ
  VIN: VCC2.+, REG2.Vin, PIR2.VDD
  N10: R1.Pin_0, LED1.anode
  N11: R2.Pin_1, LED2.anode

custom parts:
  NRF24L01: NRF24L01 module
