# Fritzing sketch nRF24l01p_uno_test_with_PIR_rx (saved by Fritzing 0.9.2b)
breadboards: 1

parts:
  NRF24L1 = NRF24L01
  Part2 = Arduino Uno (Rev3)

nets:
  VCC: NRF24L1.VCC, Part2.3V3
  N1: NRF24L1.CSN, Part2.D10_PWM/SS
  N2: NRF24L1.MOSI, Part2.D11_PWM/MOSI
  N3: NRF24L1.IRQ, Part2.D2
  GND: NRF24L1.GND, Part2.GND
  N4: NRF24L1.CE, Part2.D9_PWM
  N5: NRF24L1.SCK, Part2.D13/SCK
  N6: NRF24L1.MISO, Part2.D12/MISO

custom parts:
  NRF24L01: NRF24L01 module
