# Fritzing sketch nRF_pro_mini_test (saved by Fritzing 0.9.2b)
breadboards: 1

parts:
  Part1 = Arduino Pro Mini v13
  NRF24L1 = NRF24L01

nets:
  GND: Part1.GND, NRF24L1.GND
  VCC: Part1.VCC, NRF24L1.VCC
  N1: Part1.D13/SCK, NRF24L1.SCK
  N2: Part1.D12/MISO, NRF24L1.MISO
  N3: Part1.D11_PWM/MOSI, NRF24L1.MOSI
  N4: Part1.D10_PWM/SS, NRF24L1.CSN
  N5: Part1.D9_PWM, NRF24L1.CE
  N6: Part1.D2, NRF24L1.IRQ

custom parts:
  NRF24L01: NRF24L01 module
