# Fritzing sketch nRF_three_node_test_sender_mag_switch (saved by Fritzing 0.9.2b)
breadboards: 1

parts:
  NRF24L1 = NRF24L01
  Part2 = Arduino Uno (Rev3)
  R1 = Resistor [tolerance=±5% resistance=220 package=THT]
  S2 = Reed switch [package=THT]
  LED1 = LED - 5mm [color="Red (633nm)" package="5 mm [THT]"]

nets:
  VCC: NRF24L1.VCC, Part2.3V3, S2.pin_2
  N1: NRF24L1.CSN, Part2.D10_PWM/SS
  N2: NRF24L1.MOSI, Part2.D11_PWM/MOSI
  N3: NRF24L1.IRQ, Part2.D2
  GND: NRF24L1.GND, Part2.GND, R1.Pin_1, LED1.cathode
  N4: NRF24L1.CE, Part2.D9_PWM
  N5: NRF24L1.SCK, Part2.D13/SCK
  N6: NRF24L1.MISO, Part2.D12/MISO
  N7: Part2.D8, LED1.anode
  N8: Part2.D3_PWM, R1.Pin_0, S2.pin_1

custom parts:
  NRF24L01: NRF24L01 module
