# Fritzing sketch relay_test (saved by Fritzing 0.9.2b)
circuit board: 8.46667cm x 5.64444cm
breadboards: 1

parts:
  J1 = Piezo Speaker
  U2 = RELAY-2 [package=relay-g5v]
  D1 = Schottky Diode [part_number=1N5817 package="300 mil [THT]"]
  Q1 = NPN-Transistor [package="TO92 [THT]"]
  1000_Ohm = Resistor [tolerance=±5% resistance=220 package=THT]
  Part1 = Arduino Uno (Rev3)

nets:
  N1: J1.pin1, Q1.E, Part1.GND
  N2: J1.pin2, U2.1
  N3: U2.6, U2.10, D1.cathode, Part1.5V
  N4: U2.9, D1.anode, Q1.B
  N5: Q1.C, 1000_Ohm.Pin_0
  N6: 1000_Ohm.Pin_1, Part1.D8
